# Fritzing sketch pull_down (saved by Fritzing 0.9.3b)
breadboards: 1

parts:
  Raspberry_Pi_1 = Raspberry Pi 3 [part_number=RPI-3-V1.2]
  S1 = Pushbutton [package="[THT]"]

nets:
  N1: Raspberry_Pi_1.GIPO4, S1.Pin_1, S1.Pin_2
  N2: Raspberry_Pi_1.3V3, S1.Pin_3, S1.Pin_4
